// Logisim project 1.circ as structural Verilog: 1 circuit, main circuit main
module main (
);

  wire and_1_out, and_2_out, and_3_out, and_4_out, and_5_out, and_6_out, and_7_out, and_8_out, not_1_out,
       not_2_out, not_3_out, or_1_out;

  not not_1 (not_1_out, 1'b0);
  not not_2 (not_2_out, 1'b1);
  not not_3 (not_3_out, 1'b0);
  and and_1 (and_1_out, 1'b1, not_3_out, not_1_out, not_2_out);
  and and_2 (and_2_out, not_2_out, 1'b1, 1'b0, not_1_out);
  and and_3 (and_3_out, 1'b1, not_3_out, 1'b0, not_2_out);
  and and_4 (and_4_out, not_2_out, 1'b0, 1'b1, 1'b0);
  and and_5 (and_5_out, 1'b1, not_3_out, not_1_out, 1'b1);
  and and_6 (and_6_out, 1'b1, 1'b0, not_1_out, 1'b0);
  and and_7 (and_7_out, 1'b1, 1'b0, not_3_out, 1'b0);
  and and_8 (and_8_out, 1'b1, 1'b0, 1'b0, 1'b0);
  or or_1 (or_1_out, and_1_out, and_2_out, and_3_out, and_4_out, and_5_out, and_6_out, and_7_out, and_8_out);
  LED led_1 (.in(or_1_out));
endmodule
