// Logisim project 8x3_Encoder.circ as structural Verilog: 1 circuit, main circuit main
module main (
);

  wire or_1_out, or_2_out, or_3_out;

  or or_1 (or_1_out, 1'b0, 1'b0, 1'b0, 1'b0);
  or or_2 (or_2_out, 1'b0, 1'b0, 1'b1, 1'b0);
  or or_3 (or_3_out, 1'b0, 1'b0, 1'b1, 1'b0);
  LED Y2 (.in(or_3_out));
  LED Y1 (.in(or_2_out));
  LED Y0 (.in(or_1_out));
endmodule
